// Logisim project L20 Computer.circ as structural Verilog
module main (
  input  [6:0] Debug_Addr,
  input  Reset
);

  wire and_1_out, and_2_out, and_3_out, and_4_out, and_5_out, and_6_out, and_7_out, and_8_out, and_9_out,
       buffer_1_out, Clock_out, comparator_1_eq, comparator_2_eq, comparator_3_gt,
       conditionallogic_1_execute, counter_1_q, counter_2_q, decoder_1_out0, decoder_1_out1, decoder_2_out0,
       decoder_2_out1, decoder_2_out2, decoder_2_out3, decoder_2_out4, decoder_2_out5, decoder_2_out6,
       decoder_2_out7, decoder_2_out8, decoder_2_out9, decoder_2_out10, decoder_2_out11, disablegate_1_out,
       disablegate_2_out, disablegate_3_out, disablegate_4_out, interruptcontroller_1_handle,
       interruptcontroller_1_type, iocontroller_1_kbenable, iocontroller_1_kbread, iocontroller_1_ttyenable,
       iocontroller_1_writedisk, keyboard_1_avail, not_1_out, not_2_out, not_3_out, not_4_out, or_1_out,
       or_2_out, or_3_out, or_4_out, or_5_out, or_6_out, or_7_out;
  wire [3:0] ALU_v, Register_File_debug_out_2, Register_File_debug_out_3, Register_File_debug_out_4, V_q;
  wire [6:0] iocontroller_1_ttyout, keyboard_1_data;
  wire [7:0] FlagControl_flags_out, register_1_q_2;
  wire [23:0] adder_1_out, adder_2_out, bit_extender_1_out, bit_extender_2_out,
       interruptcontroller_1_handleaddress, multiplexer_1_out, multiplexer_2_out, PC_q, register_1_q,
       Register_File_pc_out, Register_File_sp_out, SP_q;
  wire [31:0] ALU_result, data_in_src_1_data_out, iocontroller_1_dataout, iocontroller_1_diskaddr,
       iocontroller_1_diskdataout, multiplexer_3_out, ram_1_data, ram_2_data, ram_3_data, Register_File_rd,
       Register_File_rm, Register_File_rn, rom_1_data, shifter_1_data_out;
  wire [31:12] Register_File_debug_out;

  Adder #(.width(24)) adder_1 (
    .a({register_1_q_2[3:0], register_1_q[19:0]}), .b(Register_File_pc_out), .out(adder_1_out));  // open: cin, cout
  Comparator #(.width(24), .mode("unsigned")) comparator_1 (
    .a(Register_File_pc_out), .b(adder_2_out), .eq(comparator_1_eq));  // open: gt, lt
  not not_1 (not_1_out, comparator_1_eq);
  Clock Clock (.out(Clock_out));
  Counter #(.width(1), .max('h1)) counter_1 (
    .count(and_2_out), .Q(counter_1_q), .clk(and_3_out), .clr(Reset));  // open: load, D, carry
  and and_1 (and_1_out, counter_1_q, and_2_out);
  Multiplexer #(.width(24), .enable("false")) multiplexer_1 (
    .in0(adder_1_out), .in1(Register_File_pc_out), .out(multiplexer_1_out), .sel(not_1_out));
  Multiplexer #(.width(24), .enable("false")) multiplexer_2 (
    .in0(multiplexer_1_out), .in1(interruptcontroller_1_handleaddress), .out(multiplexer_2_out),
    .sel(decoder_1_out1));
  DisableGate disablegate_1 (.In(Clock_out), .Out(disablegate_1_out), .Disable(and_1_out));
  DisableGate disablegate_2 (.In(Clock_out), .Out(disablegate_2_out), .Disable(decoder_1_out0));
  and and_2 (and_2_out, or_1_out, not_2_out);
  or or_1 (or_1_out, decoder_1_out1, not_1_out, and_9_out);
  Counter #(.width(1), .max('h1), .ongoal("stay")) counter_2 (
    .count(disablegate_2_out), .Q(counter_2_q), .clk(disablegate_2_out), .clr(Reset));  // open: load, D, carry
  Decoder #(.disabled(0)) decoder_1 (
    .out0(decoder_1_out0), .out1(decoder_1_out1), .sel(interruptcontroller_1_type),
    .en(interruptcontroller_1_handle));
  InterruptController interruptcontroller_1 (
    .Call_Clear(and_5_out), .InrCode(register_1_q_2), .Set(and_4_out), .Type(interruptcontroller_1_type),
    .HandleAddress(interruptcontroller_1_handleaddress), .Value(Register_File_rm), .Reset(Reset),
    .Handle(interruptcontroller_1_handle));  // open: Priority
  ROM #(.addrWidth(24), .dataWidth(32)) rom_1 (.addr(PC_q), .data(rom_1_data));  // open: sel
  DisableGate disablegate_3 (.In(disablegate_2_out), .Out(disablegate_3_out), .Disable(counter_1_q));
  Counter #(.width(24), .max('hffffff), .ongoal("stay")) PC (
    .load(and_1_out), .D(multiplexer_2_out), .count(disablegate_1_out), .Q(PC_q), .clk(disablegate_2_out),
    .clr(Reset));  // open: carry
  Comparator #(.width(24), .mode("unsigned")) comparator_2 (
    .a(Register_File_sp_out), .b(SP_q), .eq(comparator_2_eq));  // open: gt, lt
  not not_2 (not_2_out, disablegate_2_out);
  or or_2 (or_2_out, not_3_out, decoder_2_out9);
  not not_3 (not_3_out, comparator_2_eq);
  and and_3 (and_3_out, counter_2_q, not_2_out);
  and and_4 (and_4_out, and_3_out, decoder_2_out1);
  and and_5 (and_5_out, decoder_2_out0, and_3_out);
  Register #(.width(32)) register_1 (
    .D(rom_1_data), .en(disablegate_2_out), .Q({register_1_q[23:20], register_1_q_2, register_1_q[19:0]}),
    .clk(disablegate_3_out), .clr(Reset));
  and and_6 (and_6_out, or_4_out, disablegate_2_out);
  Adder #(.width(24)) adder_2 (.a(PC_q), .b(24'h1), .out(adder_2_out));  // open: cin, cout
  Counter #(.width(24), .max('hffffff), .ongoal("stay")) SP (
    .load(or_2_out), .D(Register_File_sp_out), .count(and_7_out), .Q(SP_q), .clk(buffer_1_out), .clr(Reset));  // open: carry
  buf buffer_1 (buffer_1_out, and_3_out);
  or or_3 (or_3_out, decoder_2_out6, decoder_2_out9);
  reg128 Register_File (
    .An({register_1_q_2[0], register_1_q[19:14]}), .Am(register_1_q[6:0]), .Ad(register_1_q_2[7:1]),
    .Data_In(data_in_src_1_data_out), .Debug_Addr(Debug_Addr), .Rn(Register_File_rn), .Rm(Register_File_rm),
    .Rd(Register_File_rd),
    .Debug_Out({Register_File_debug_out, Register_File_debug_out_2, Register_File_debug_out_3, Register_File_debug_out_4}),
    .Clock(buffer_1_out), .Reset(Reset), .WriteEn(and_6_out), .SP_In(SP_q), .SP_out(Register_File_sp_out),
    .PC_In(adder_2_out), .PC_out(Register_File_pc_out));
  and and_7 (and_7_out, and_3_out, or_3_out);
  Data_In_Src data_in_src_1 (
    .Memory_In(multiplexer_3_out), .ALU_In(ALU_result), .Stack_In(ram_1_data), .Shift_In(shifter_1_data_out),
    .Data_Out(data_in_src_1_data_out), .M(decoder_2_out2), .ALU(or_6_out), .St(decoder_2_out9),
    .Sh(decoder_2_out10));
  or or_4 (or_4_out, decoder_2_out10, decoder_2_out9, or_6_out, decoder_2_out2);
  not not_4 (not_4_out, and_3_out);
  FlagControl FlagControl (
    .Flags_in(ALU_v), .Mask(register_1_q_2[7:4]), .Flags_Out(FlagControl_flags_out), .ALU(or_5_out),
    .Set(decoder_2_out7), .Clear(decoder_2_out8));
  and and_8 (and_8_out, decoder_2_out4, V_q[1]);
  ALU ALU (
    .A(Register_File_rn), .B(Register_File_rm), .Result(ALU_result), .Carry_In(and_8_out),
    .Control(decoder_2_out5), .N(ALU_v[3]), .Z(ALU_v[2]), .C(ALU_v[1]), .V(ALU_v[0]));
  or or_5 (or_5_out, decoder_2_out5, decoder_2_out4);
  Shifter shifter_1 (
    .Data_In(Register_File_rn), .RegShiftIn(Register_File_rm), .Imm12(register_1_q[11:0]),
    .Imm5(register_1_q[18:14]), .Data_Out(shifter_1_data_out), .Shift_Control(register_1_q[13:12]));
  or or_6 (or_6_out, decoder_2_out5, decoder_2_out4);
  RAM #(.addrWidth(24), .dataWidth(32), .bus("separate")) ram_1 (
    .addr(SP_q), .din(Register_File_rd), .data(ram_1_data), .str(decoder_2_out6), .clk(not_4_out), .clr(Reset));  // open: sel, ld
  Decoder #(.select(4)) decoder_2 (
    .out0(decoder_2_out0), .out1(decoder_2_out1), .out2(decoder_2_out2), .out3(decoder_2_out3),
    .out4(decoder_2_out4), .out5(decoder_2_out5), .out6(decoder_2_out6), .out7(decoder_2_out7),
    .out8(decoder_2_out8), .out9(decoder_2_out9), .out10(decoder_2_out10), .out11(decoder_2_out11),
    .sel(register_1_q[23:20]));  // open: out12, out13, out14, out15, en
  ConditionalLogic conditionallogic_1 (
    .Condition(register_1_q_2[7:4]), .N(V_q[3]), .Z(V_q[2]), .C(V_q[1]), .V(V_q[0]),
    .Execute(conditionallogic_1_execute));
  Register #(.width(1)) N (
    .D(FlagControl_flags_out[6]), .en(FlagControl_flags_out[7]), .Q(V_q[3]), .clk(and_3_out), .clr(Reset));
  Register #(.width(1)) Z (
    .D(FlagControl_flags_out[4]), .en(FlagControl_flags_out[5]), .Q(V_q[2]), .clk(and_3_out), .clr(Reset));
  Register #(.width(1)) C (
    .D(FlagControl_flags_out[2]), .en(FlagControl_flags_out[3]), .Q(V_q[1]), .clk(and_3_out), .clr(Reset));
  Register #(.width(1)) V (
    .D(FlagControl_flags_out[0]), .en(FlagControl_flags_out[1]), .Q(V_q[0]), .clk(and_3_out), .clr(Reset));
  Comparator #(.width(32), .mode("unsigned")) comparator_3 (
    .a(ALU_result), .b(32'hffffff), .gt(comparator_3_gt));  // open: eq, lt
  Multiplexer #(.width(32), .enable("false")) multiplexer_3 (
    .in0(ram_2_data), .in1(iocontroller_1_dataout), .out(multiplexer_3_out), .sel(comparator_3_gt));
  and and_9 (and_9_out, conditionallogic_1_execute, decoder_2_out11);
  Hex_Digit_Display hex_digit_display_1 (.value(Register_File_debug_out[31:28]));  // open: dp
  Hex_Digit_Display hex_digit_display_2 (.value(Register_File_debug_out[27:24]));  // open: dp
  DisableGate disablegate_4 (.In(decoder_2_out3), .Out(disablegate_4_out), .Disable(comparator_3_gt));
  Bit_Extender #(.in_width(32), .out_width(24)) bit_extender_1 (.in(ALU_result), .out(bit_extender_1_out));
  IOController iocontroller_1 (
    .Write(decoder_2_out3), .Address(ALU_result), .DataIn(Register_File_rd), .KBIn(keyboard_1_data),
    .KBNotEmpty(keyboard_1_avail), .Read(decoder_2_out2), .ExeClock(and_3_out), .Reset(Reset),
    .TTYOut(iocontroller_1_ttyout), .TTYEnable(iocontroller_1_ttyenable), .KBEnable(iocontroller_1_kbenable),
    .DataOut(iocontroller_1_dataout), .KBRead(iocontroller_1_kbread), .DiskDataIn(ram_3_data),
    .DiskAddr(iocontroller_1_diskaddr), .DiskDataOut(iocontroller_1_diskdataout),
    .WriteDisk(iocontroller_1_writedisk));
  Bit_Extender #(.in_width(32), .out_width(24)) bit_extender_2 (.in(iocontroller_1_diskaddr), .out(bit_extender_2_out));
  Hex_Digit_Display hex_digit_display_3 (.value(Register_File_debug_out[19:16]));  // open: dp
  Hex_Digit_Display hex_digit_display_4 (.value(Register_File_debug_out[23:20]));  // open: dp
  Hex_Digit_Display hex_digit_display_5 (.value(Register_File_debug_out[15:12]));  // open: dp
  Hex_Digit_Display hex_digit_display_6 (.value(Register_File_debug_out_2));  // open: dp
  RAM #(.addrWidth(24), .dataWidth(32), .bus("separate")) ram_2 (
    .addr(bit_extender_1_out), .din(Register_File_rd), .data(ram_2_data), .str(disablegate_4_out),
    .clk(and_3_out));  // open: sel, ld, clr
  TTY tty_1 (.data(iocontroller_1_ttyout), .clk(and_3_out), .we(iocontroller_1_ttyenable), .clr(Reset));
  Keyboard keyboard_1 (
    .clk(and_3_out), .re(iocontroller_1_kbread), .clr(or_7_out), .avail(keyboard_1_avail),
    .data(keyboard_1_data));
  RAM #(.addrWidth(24), .dataWidth(32), .bus("separate")) ram_3 (
    .addr(bit_extender_2_out), .din(iocontroller_1_diskdataout), .data(ram_3_data),
    .str(iocontroller_1_writedisk), .clk(and_3_out));  // open: sel, ld, clr
  Hex_Digit_Display hex_digit_display_7 (.value(Register_File_debug_out_4));  // open: dp
  Hex_Digit_Display hex_digit_display_8 (.value(Register_File_debug_out_3));  // open: dp
  or or_7 (or_7_out, ~iocontroller_1_kbenable, Reset);  // OR_Gate

  // Notes on the sheet:
  //   contents of rom_1 (hex, n*v repeats v):
  //   b0000003 4*0 b0fffff9
endmodule

module reg32 (
  input  Reset,
  input  Clock,
  input  [31:0] Data_In,
  input  [4:0] An,
  input  [4:0] Am,
  input  [4:0] Rd,
  input  WriteEnable,
  input  [4:0] Ak,
  input  [4:0] DebugAddr,
  output [31:0] Rn,
  output [31:0] Rm,
  output [31:0] Rk,
  output [31:0] Debug_Out
);

  wire decoder_1_out0, decoder_1_out1, decoder_1_out2, decoder_1_out3, decoder_2_out0, decoder_2_out1,
       decoder_2_out2, decoder_2_out3, decoder_3_out0, decoder_3_out1, decoder_3_out2, decoder_3_out3,
       decoder_4_out0, decoder_4_out1, decoder_4_out2, decoder_4_out3, decoder_5_out0, decoder_5_out1,
       decoder_5_out2, decoder_5_out3, decoder_5_out4, decoder_5_out5, decoder_5_out6, decoder_5_out7,
       decoder_6_out0, decoder_6_out1, decoder_6_out2, decoder_6_out3, decoder_7_out0, decoder_7_out1,
       decoder_7_out2, decoder_7_out3, decoder_8_out0, decoder_8_out1, decoder_8_out2, decoder_8_out3,
       decoder_9_out0, decoder_9_out1, decoder_9_out2, decoder_9_out3;
  wire [31:0] multiplexer_2_out, multiplexer_3_out, multiplexer_4_out, multiplexer_5_out, multiplexer_6_out,
       multiplexer_7_out, multiplexer_8_out, multiplexer_9_out, register_1_q, register_2_q, register_3_q,
       register_4_q, register_5_q, register_6_q, register_7_q, register_8_q, register_9_q, register_10_q,
       register_11_q, register_12_q, register_13_q, register_14_q, register_15_q, register_16_q,
       register_17_q, register_18_q, register_19_q, register_20_q, register_21_q, register_22_q,
       register_23_q, register_24_q, register_25_q, register_26_q, register_27_q, register_28_q,
       register_29_q, register_30_q, register_31_q, register_32_q;

  Decoder #(.select(2), .disabled(0)) decoder_1 (
    .out0(decoder_1_out0), .out1(decoder_1_out1), .out2(decoder_1_out2), .out3(decoder_1_out3),
    .sel(Rd[4:3]), .en(decoder_5_out0));
  Register #(.width(32)) register_1 (.D(Data_In), .en(decoder_1_out0), .Q(register_1_q), .clk(Clock), .clr(Reset));
  Register #(.width(32)) register_2 (.D(Data_In), .en(decoder_1_out1), .Q(register_2_q), .clk(Clock), .clr(Reset));
  Register #(.width(32)) register_3 (.D(Data_In), .en(decoder_1_out2), .Q(register_3_q), .clk(Clock), .clr(Reset));
  Register #(.width(32)) register_4 (.D(Data_In), .en(decoder_1_out3), .Q(register_4_q), .clk(Clock), .clr(Reset));
  Decoder #(.select(2), .disabled(0)) decoder_2 (
    .out0(decoder_2_out0), .out1(decoder_2_out1), .out2(decoder_2_out2), .out3(decoder_2_out3),
    .sel(Rd[4:3]), .en(decoder_5_out1));
  Register #(.width(32)) register_5 (.D(Data_In), .en(decoder_2_out0), .Q(register_5_q), .clk(Clock), .clr(Reset));
  Register #(.width(32)) register_6 (.D(Data_In), .en(decoder_2_out1), .Q(register_6_q), .clk(Clock), .clr(Reset));
  Register #(.width(32)) register_7 (.D(Data_In), .en(decoder_2_out2), .Q(register_7_q), .clk(Clock), .clr(Reset));
  Register #(.width(32)) register_8 (.D(Data_In), .en(decoder_2_out3), .Q(register_8_q), .clk(Clock), .clr(Reset));
  Decoder #(.select(2), .disabled(0)) decoder_3 (
    .out0(decoder_3_out0), .out1(decoder_3_out1), .out2(decoder_3_out2), .out3(decoder_3_out3),
    .sel(Rd[4:3]), .en(decoder_5_out2));
  Register #(.width(32)) register_9 (.D(Data_In), .en(decoder_3_out0), .Q(register_9_q), .clk(Clock), .clr(Reset));
  Register #(.width(32)) register_10 (.D(Data_In), .en(decoder_3_out1), .Q(register_10_q), .clk(Clock), .clr(Reset));
  Register #(.width(32)) register_11 (.D(Data_In), .en(decoder_3_out2), .Q(register_11_q), .clk(Clock), .clr(Reset));
  Register #(.width(32)) register_12 (.D(Data_In), .en(decoder_3_out3), .Q(register_12_q), .clk(Clock), .clr(Reset));
  Decoder #(.select(2), .disabled(0)) decoder_4 (
    .out0(decoder_4_out0), .out1(decoder_4_out1), .out2(decoder_4_out2), .out3(decoder_4_out3),
    .sel(Rd[4:3]), .en(decoder_5_out3));
  Decoder #(.select(3), .disabled(0)) decoder_5 (
    .out0(decoder_5_out0), .out1(decoder_5_out1), .out2(decoder_5_out2), .out3(decoder_5_out3),
    .out4(decoder_5_out4), .out5(decoder_5_out5), .out6(decoder_5_out6), .out7(decoder_5_out7),
    .sel(Rd[2:0]), .en(WriteEnable));
  Register #(.width(32)) register_13 (.D(Data_In), .en(decoder_4_out0), .Q(register_13_q), .clk(Clock), .clr(Reset));
  Register #(.width(32)) register_14 (.D(Data_In), .en(decoder_4_out1), .Q(register_14_q), .clk(Clock), .clr(Reset));
  Register #(.width(32)) register_15 (.D(Data_In), .en(decoder_4_out2), .Q(register_15_q), .clk(Clock), .clr(Reset));
  Register #(.width(32)) register_16 (.D(Data_In), .en(decoder_4_out3), .Q(register_16_q), .clk(Clock), .clr(Reset));
  Decoder #(.select(2), .disabled(0)) decoder_6 (
    .out0(decoder_6_out0), .out1(decoder_6_out1), .out2(decoder_6_out2), .out3(decoder_6_out3),
    .sel(Rd[4:3]), .en(decoder_5_out4));
  Register #(.width(32)) register_17 (.D(Data_In), .en(decoder_6_out0), .Q(register_17_q), .clk(Clock), .clr(Reset));
  Register #(.width(32)) register_18 (.D(Data_In), .en(decoder_6_out1), .Q(register_18_q), .clk(Clock), .clr(Reset));
  Register #(.width(32)) register_19 (.D(Data_In), .en(decoder_6_out2), .Q(register_19_q), .clk(Clock), .clr(Reset));
  Register #(.width(32)) register_20 (.D(Data_In), .en(decoder_6_out3), .Q(register_20_q), .clk(Clock), .clr(Reset));
  Decoder #(.select(2), .disabled(0)) decoder_7 (
    .out0(decoder_7_out0), .out1(decoder_7_out1), .out2(decoder_7_out2), .out3(decoder_7_out3),
    .sel(Rd[4:3]), .en(decoder_5_out5));
  Register #(.width(32)) register_21 (.D(Data_In), .en(decoder_7_out0), .Q(register_21_q), .clk(Clock), .clr(Reset));
  Register #(.width(32)) register_22 (.D(Data_In), .en(decoder_7_out1), .Q(register_22_q), .clk(Clock), .clr(Reset));
  Register #(.width(32)) register_23 (.D(Data_In), .en(decoder_7_out2), .Q(register_23_q), .clk(Clock), .clr(Reset));
  Register #(.width(32)) register_24 (.D(Data_In), .en(decoder_7_out3), .Q(register_24_q), .clk(Clock), .clr(Reset));
  Decoder #(.select(2), .disabled(0)) decoder_8 (
    .out0(decoder_8_out0), .out1(decoder_8_out1), .out2(decoder_8_out2), .out3(decoder_8_out3),
    .sel(Rd[4:3]), .en(decoder_5_out6));
  Register #(.width(32)) register_25 (.D(Data_In), .en(decoder_8_out0), .Q(register_25_q), .clk(Clock), .clr(Reset));
  Register #(.width(32)) register_26 (.D(Data_In), .en(decoder_8_out1), .Q(register_26_q), .clk(Clock), .clr(Reset));
  Register #(.width(32)) register_27 (.D(Data_In), .en(decoder_8_out2), .Q(register_27_q), .clk(Clock), .clr(Reset));
  Register #(.width(32)) register_28 (.D(Data_In), .en(decoder_8_out3), .Q(register_28_q), .clk(Clock), .clr(Reset));
  Decoder #(.select(2), .disabled(0)) decoder_9 (
    .out0(decoder_9_out0), .out1(decoder_9_out1), .out2(decoder_9_out2), .out3(decoder_9_out3),
    .sel(Rd[4:3]), .en(decoder_5_out7));
  Register #(.width(32)) register_29 (.D(Data_In), .en(decoder_9_out0), .Q(register_29_q), .clk(Clock), .clr(Reset));
  Register #(.width(32)) register_30 (.D(Data_In), .en(decoder_9_out1), .Q(register_30_q), .clk(Clock), .clr(Reset));
  Register #(.width(32)) register_31 (.D(Data_In), .en(decoder_9_out2), .Q(register_31_q), .clk(Clock), .clr(Reset));
  Register #(.width(32)) register_32 (.D(Data_In), .en(decoder_9_out3), .Q(register_32_q), .clk(Clock), .clr(Reset));
  Multiplexer #(.select(5), .width(32)) multiplexer_1 (
    .in0(register_1_q), .in1(register_5_q), .in2(register_9_q), .in3(register_13_q), .in4(register_17_q),
    .in5(register_21_q), .in6(register_25_q), .in7(register_29_q), .in8(register_2_q), .in9(register_6_q),
    .in10(register_10_q), .in11(register_14_q), .in12(register_18_q), .in13(register_22_q),
    .in14(register_26_q), .in15(register_30_q), .in16(register_3_q), .in17(register_7_q),
    .in18(register_11_q), .in19(register_15_q), .in20(register_19_q), .in21(register_23_q),
    .in22(register_27_q), .in23(register_31_q), .in24(register_4_q), .in25(register_8_q),
    .in26(register_12_q), .in27(register_16_q), .in28(register_20_q), .in29(register_24_q),
    .in30(register_28_q), .in31(register_32_q), .out(Debug_Out), .sel(DebugAddr));  // open: en
  Multiplexer #(.select(3), .width(32)) multiplexer_2 (
    .in0(register_1_q), .in1(register_5_q), .in2(register_9_q), .in3(register_13_q), .in4(register_17_q),
    .in5(register_21_q), .in6(register_25_q), .in7(register_29_q), .out(multiplexer_2_out), .sel(An[2:0]));  // open: en
  Multiplexer #(.select(3), .width(32)) multiplexer_3 (
    .in0(register_1_q), .in1(register_5_q), .in2(register_9_q), .in3(register_13_q), .in4(register_17_q),
    .in5(register_21_q), .in6(register_25_q), .in7(register_29_q), .out(multiplexer_3_out), .sel(Am[2:0]));  // open: en
  Multiplexer #(.select(3), .width(32)) multiplexer_4 (
    .in0(register_2_q), .in1(register_6_q), .in2(register_10_q), .in3(register_14_q), .in4(register_18_q),
    .in5(register_22_q), .in6(register_26_q), .in7(register_30_q), .out(multiplexer_4_out), .sel(An[2:0]));  // open: en
  Multiplexer #(.select(3), .width(32)) multiplexer_5 (
    .in0(register_2_q), .in1(register_6_q), .in2(register_10_q), .in3(register_14_q), .in4(register_18_q),
    .in5(register_22_q), .in6(register_26_q), .in7(register_30_q), .out(multiplexer_5_out), .sel(Am[2:0]));  // open: en
  Multiplexer #(.select(3), .width(32)) multiplexer_6 (
    .in0(register_3_q), .in1(register_7_q), .in2(register_11_q), .in3(register_15_q), .in4(register_19_q),
    .in5(register_23_q), .in6(register_27_q), .in7(register_31_q), .out(multiplexer_6_out), .sel(An[2:0]));  // open: en
  Multiplexer #(.select(3), .width(32)) multiplexer_7 (
    .in0(register_3_q), .in1(register_7_q), .in2(register_11_q), .in3(register_15_q), .in4(register_19_q),
    .in5(register_23_q), .in6(register_27_q), .in7(register_31_q), .out(multiplexer_7_out), .sel(Am[2:0]));  // open: en
  Multiplexer #(.select(3), .width(32)) multiplexer_8 (
    .in0(register_4_q), .in1(register_8_q), .in2(register_12_q), .in3(register_16_q), .in4(register_20_q),
    .in5(register_24_q), .in6(register_28_q), .in7(register_32_q), .out(multiplexer_8_out), .sel(An[2:0]));  // open: en
  Multiplexer #(.select(3), .width(32)) multiplexer_9 (
    .in0(register_4_q), .in1(register_8_q), .in2(register_12_q), .in3(register_16_q), .in4(register_20_q),
    .in5(register_24_q), .in6(register_28_q), .in7(register_32_q), .out(multiplexer_9_out), .sel(Am[2:0]));  // open: en
  Multiplexer #(.select(5), .width(32)) multiplexer_10 (
    .in0(register_1_q), .in1(register_5_q), .in2(register_9_q), .in3(register_13_q), .in4(register_17_q),
    .in5(register_21_q), .in6(register_25_q), .in7(register_29_q), .in8(register_2_q), .in9(register_6_q),
    .in10(register_10_q), .in11(register_14_q), .in12(register_18_q), .in13(register_22_q),
    .in14(register_26_q), .in15(register_30_q), .in16(register_3_q), .in17(register_7_q),
    .in18(register_11_q), .in19(register_15_q), .in20(register_19_q), .in21(register_23_q),
    .in22(register_27_q), .in23(register_31_q), .in24(register_4_q), .in25(register_8_q),
    .in26(register_12_q), .in27(register_16_q), .in28(register_20_q), .in29(register_24_q),
    .in30(register_28_q), .in31(register_32_q), .out(Rk), .sel(Ak));  // open: en
  Multiplexer #(.select(2), .width(32)) multiplexer_11 (
    .in0(multiplexer_2_out), .in1(multiplexer_4_out), .in2(multiplexer_6_out), .in3(multiplexer_8_out),
    .out(Rn), .sel(An[4:3]));  // open: en
  Multiplexer #(.select(2), .width(32)) multiplexer_12 (
    .in0(multiplexer_3_out), .in1(multiplexer_5_out), .in2(multiplexer_7_out), .in3(multiplexer_9_out),
    .out(Rm), .sel(Am[4:3]));  // open: en
endmodule

module reg128 (
  input  Clock,
  input  Reset,
  input  WriteEn,
  input  [6:0] An,
  input  [6:0] Am,
  input  [6:0] Ad,
  input  [31:0] Data_In,
  input  [6:0] Debug_Addr,
  input  [23:0] SP_In,
  input  [23:0] PC_In,
  output [31:0] Rn,
  output [31:0] Rm,
  output [31:0] Rd,
  output [31:0] Debug_Out,
  output [23:0] SP_out,
  output [23:0] PC_out
);

  wire addresshelp_3_writable, and_1_out, and_2_out, and_3_out, decoder_1_out0, decoder_1_out1,
       decoder_1_out2, decoder_1_out3;
  wire [1:0] addresshelp_1_select, addresshelp_1_value, addresshelp_2_select, addresshelp_2_value,
       addresshelp_3_select, addresshelp_3_value, addresshelp_4_select, addresshelp_4_value;
  wire [31:0] bit_extender_1_out, bit_extender_2_out, bit_extender_5_out, bit_extender_6_out,
       bit_extender_7_out, bit_extender_8_out, multiplexer_1_out, multiplexer_2_out, multiplexer_3_out,
       multiplexer_4_out, multiplexer_5_out, multiplexer_6_out, reg32_1_debug_out, reg32_1_rk, reg32_1_rm,
       reg32_1_rn, reg32_2_debug_out, reg32_2_rk, reg32_2_rm, reg32_2_rn, reg32_3_debug_out, reg32_3_rk,
       reg32_3_rm, reg32_3_rn, reg32_4_debug_out, reg32_4_rk, reg32_4_rm, reg32_4_rn;

  AddressHelp addresshelp_1 (.Addr(An), .Value(addresshelp_1_value), .Select(addresshelp_1_select));  // open: Writable
  AddressHelp addresshelp_2 (.Addr(Am), .Value(addresshelp_2_value), .Select(addresshelp_2_select));  // open: Writable
  AddressHelp addresshelp_3 (
    .Addr(Ad), .Writable(addresshelp_3_writable), .Value(addresshelp_3_value), .Select(addresshelp_3_select));
  assign bit_extender_1_out = {{8{1'b0}}, SP_In};  // Bit_Extender bit_extender_1
  assign bit_extender_2_out = {{8{1'b0}}, PC_In};  // Bit_Extender bit_extender_2
  reg32 reg32_1 (
    .Rd(Ad[4:0]), .WriteEnable(decoder_1_out0), .DebugAddr(Debug_Addr[4:0]), .Rn(reg32_1_rn),
    .Rm(reg32_1_rm), .An(An[4:0]), .Am(Am[4:0]), .Rk(reg32_1_rk), .Ak(Ad[4:0]), .Reset(Reset), .Clock(Clock),
    .Debug_Out(reg32_1_debug_out), .Data_In(Data_In));
  reg32 reg32_2 (
    .Rd(Ad[4:0]), .WriteEnable(decoder_1_out1), .DebugAddr(Debug_Addr[4:0]), .Rn(reg32_2_rn),
    .Rm(reg32_2_rm), .An(An[4:0]), .Am(Am[4:0]), .Rk(reg32_2_rk), .Ak(Ad[4:0]), .Reset(Reset), .Clock(Clock),
    .Debug_Out(reg32_2_debug_out), .Data_In(Data_In));
  AddressHelp addresshelp_4 (
    .Addr(Debug_Addr), .Value(addresshelp_4_value), .Select(addresshelp_4_select));  // open: Writable
  and and_1 (and_1_out, addresshelp_3_writable, ~addresshelp_3_select[0], addresshelp_3_select[1]);  // AND_Gate
  and and_2 (and_2_out, addresshelp_3_writable, addresshelp_3_select[0], addresshelp_3_select[1]);
  and and_3 (and_3_out, WriteEn, addresshelp_3_writable);
  Decoder #(.select(2), .disabled(0)) decoder_1 (
    .out0(decoder_1_out0), .out1(decoder_1_out1), .out2(decoder_1_out2), .out3(decoder_1_out3),
    .sel(Ad[6:5]), .en(and_3_out));
  reg32 reg32_3 (
    .Rd(Ad[4:0]), .WriteEnable(decoder_1_out2), .DebugAddr(Debug_Addr[4:0]), .Rn(reg32_3_rn),
    .Rm(reg32_3_rm), .An(An[4:0]), .Am(Am[4:0]), .Rk(reg32_3_rk), .Ak(Ad[4:0]), .Reset(Reset), .Clock(Clock),
    .Debug_Out(reg32_3_debug_out), .Data_In(Data_In));
  Multiplexer #(.select(2), .width(32)) multiplexer_1 (
    .in0(reg32_1_debug_out), .in1(reg32_2_debug_out), .in2(reg32_3_debug_out), .in3(reg32_4_debug_out),
    .out(multiplexer_1_out), .sel(Debug_Addr[6:5]));  // open: en
  reg32 reg32_4 (
    .Rd(Ad[4:0]), .WriteEnable(decoder_1_out3), .DebugAddr(Debug_Addr[4:0]), .Rn(reg32_4_rn),
    .Rm(reg32_4_rm), .An(An[4:0]), .Am(Am[4:0]), .Rk(reg32_4_rk), .Ak(Ad[4:0]), .Reset(Reset), .Clock(Clock),
    .Debug_Out(reg32_4_debug_out), .Data_In(Data_In));
  Bit_Extender #(.in_width(32), .out_width(24)) bit_extender_3 (.in(multiplexer_2_out), .out(SP_out));
  Multiplexer #(.width(32)) multiplexer_2 (
    .in0(bit_extender_1_out), .in1(Data_In), .out(multiplexer_2_out), .sel(and_1_out));  // open: en
  Bit_Extender #(.in_width(32), .out_width(24)) bit_extender_4 (.in(multiplexer_3_out), .out(PC_out));
  Multiplexer #(.width(32)) multiplexer_3 (
    .in0(bit_extender_2_out), .in1(Data_In), .out(multiplexer_3_out), .sel(and_2_out));  // open: en
  assign bit_extender_5_out = {{30{addresshelp_4_value[1]}}, addresshelp_4_value};  // Bit_Extender bit_extender_5
  Multiplexer #(.select(2), .width(32)) multiplexer_4 (
    .in0(reg32_1_rn), .in1(reg32_2_rn), .in2(reg32_3_rn), .in3(reg32_4_rn), .out(multiplexer_4_out),
    .sel(An[6:5]));  // open: en
  Multiplexer #(.select(2), .width(32)) multiplexer_5 (
    .in0(reg32_1_rm), .in1(reg32_2_rm), .in2(reg32_3_rm), .in3(reg32_4_rm), .out(multiplexer_5_out),
    .sel(Am[6:5]));  // open: en
  Multiplexer #(.select(2), .width(32)) multiplexer_6 (
    .in0(reg32_1_rk), .in1(reg32_2_rk), .in2(reg32_3_rk), .in3(reg32_4_rk), .out(multiplexer_6_out),
    .sel(Ad[6:5]));  // open: en
  Multiplexer #(.select(2), .width(32)) multiplexer_7 (
    .in0(multiplexer_1_out), .in1(bit_extender_5_out), .in2(bit_extender_1_out), .in3(bit_extender_2_out),
    .out(Debug_Out), .sel(addresshelp_4_select));  // open: en
  assign bit_extender_6_out = {{30{addresshelp_1_value[1]}}, addresshelp_1_value};  // Bit_Extender bit_extender_6
  assign bit_extender_7_out = {{30{addresshelp_2_value[1]}}, addresshelp_2_value};  // Bit_Extender bit_extender_7
  assign bit_extender_8_out = {{30{addresshelp_3_value[1]}}, addresshelp_3_value};  // Bit_Extender bit_extender_8
  Multiplexer #(.select(2), .width(32)) multiplexer_8 (
    .in0(multiplexer_4_out), .in1(bit_extender_6_out), .in2(bit_extender_1_out), .in3(bit_extender_2_out),
    .out(Rn), .sel(addresshelp_1_select));  // open: en
  Multiplexer #(.select(2), .width(32)) multiplexer_9 (
    .in0(multiplexer_5_out), .in1(bit_extender_7_out), .in2(bit_extender_1_out), .in3(bit_extender_2_out),
    .out(Rm), .sel(addresshelp_2_select));  // open: en
  Multiplexer #(.select(2), .width(32)) multiplexer_10 (
    .in0(multiplexer_6_out), .in1(bit_extender_8_out), .in2(bit_extender_1_out), .in3(bit_extender_2_out),
    .out(Rd), .sel(addresshelp_3_select));  // open: en
endmodule

module ALU (
  input  Carry_In,
  input  Control,
  input  [31:0] A,
  input  [31:0] B,
  output [31:0] Result,
  output N,
  output Z,
  output C,
  output V
);

  wire adder_1_cout, and_2_out, not_1_out, xnor_1_out, xor_1_out;
  wire [31:0] adder_1_out, nand_1_out;

  nor nor_1 (Z, N, Result[30], Result[29], Result[28], Result[27], Result[26], Result[25], Result[24], Result[23], Result[22], Result[21], Result[20], Result[19], Result[18], Result[17], Result[16], Result[15], Result[14], Result[13], Result[12], Result[11], Result[10], Result[9], Result[8], Result[7], Result[6], Result[5], Result[4], Result[3], Result[2], Result[1], Result[0]);
  and and_1 (C, not_1_out, adder_1_cout);
  assign nand_1_out = ~(A & B);  // NAND_Gate nand_1, 32 bits wide
  Adder #(.width(32)) adder_1 (.a(A), .b(B), .out(adder_1_out), .cin(Carry_In), .cout(adder_1_cout));
  xor xor_1 (xor_1_out, A[31], N);
  xnor xnor_1 (xnor_1_out, A[31], B[31]);
  and and_2 (and_2_out, xnor_1_out, xor_1_out);
  and and_3 (V, and_2_out, not_1_out);
  not not_1 (not_1_out, Control);
  Multiplexer #(.width(32)) multiplexer_1 (
    .in0(nand_1_out), .in1(adder_1_out), .out({N, Result[30:0]}), .sel(not_1_out));  // open: en

  assign Result[31] = N;
endmodule

module FlagControl (
  input  [3:0] Flags_in,
  input  [3:0] Mask,
  input  ALU,
  input  Set,
  input  Clear,
  output [7:0] Flags_Out
);

  wire [1:0] priority_encoder_1_out;

  Priority_Encoder #(.select(2)) priority_encoder_1 (
    .in0(1'b1), .in1(ALU), .in2(Set), .in3(Clear), .out(priority_encoder_1_out));
  Multiplexer #(.select(2), .width(8)) multiplexer_1 (
    .in0({8{1'b0}}), .in1({1'b1, Flags_in[3], 1'b1, Flags_in[2], 1'b1, Flags_in[1], 1'b1, Flags_in[0]}),
    .in2({Mask[3], 1'b1, Mask[2], 1'b1, Mask[1], 1'b1, Mask[0], 1'b1}),
    .in3({Mask[3], 1'b0, Mask[2], 1'b0, Mask[1], 1'b0, Mask[0], 1'b0}), .out(Flags_Out),
    .sel(priority_encoder_1_out));  // open: en
endmodule

module Data_In_Src (
  input  [31:0] Memory_In,
  input  [31:0] ALU_In,
  input  [31:0] Stack_In,
  input  [31:0] Shift_In,
  input  M,
  input  ALU,
  input  St,
  input  Sh,
  output [31:0] Data_Out
);

  wire [1:0] priority_encoder_1_out;

  Multiplexer #(.select(2), .width(32)) multiplexer_1 (
    .in0(Memory_In), .in1(ALU_In), .in2(Stack_In), .in3(Shift_In), .out(Data_Out),
    .sel(priority_encoder_1_out));  // open: en
  Priority_Encoder #(.select(2)) priority_encoder_1 (
    .in0(M), .in1(ALU), .in2(St), .in3(Sh), .out(priority_encoder_1_out));
endmodule

module Shifter (
  input  [31:0] Data_In,
  input  [31:0] RegShiftIn,
  input  [11:0] Imm12,
  input  [4:0] Imm5,
  input  [1:0] Shift_Control,
  output [31:0] Data_Out
);

  wire and_1_out, comparator_1_gt, nand_1_out;
  wire [4:0] bit_extender_2_out;
  wire [31:0] bit_extender_1_out, multiplexer_1_out, shifter_1_out, shifter_2_out, shifter_3_out,
       shifter_4_out;

  assign bit_extender_1_out = {{20{Imm12[11]}}, Imm12};  // Bit_Extender bit_extender_1
  Shifter_part #(.width(32)) shifter_1 (.in(Data_In), .\dist (bit_extender_2_out), .out(shifter_1_out));
  Shifter_part #(.width(32), .shift("lr")) shifter_2 (.in(Data_In), .\dist (bit_extender_2_out), .out(shifter_2_out));
  Shifter_part #(.width(32), .shift("ar")) shifter_3 (.in(Data_In), .\dist (bit_extender_2_out), .out(shifter_3_out));
  Bit_Extender #(.in_width(32), .out_width(5)) bit_extender_2 (.in(RegShiftIn), .out(bit_extender_2_out));
  Shifter_part #(.width(32)) shifter_4 (.in(bit_extender_1_out), .\dist (Imm5), .out(shifter_4_out));
  Comparator #(.width(32)) comparator_1 (.a(RegShiftIn), .b(32'h1f), .gt(comparator_1_gt));  // open: eq, lt
  and and_1 (and_1_out, nand_1_out, comparator_1_gt);
  nand nand_1 (nand_1_out, Shift_Control[1], Shift_Control[0]);
  Multiplexer #(.select(2), .width(32)) multiplexer_1 (
    .in0(shifter_1_out), .in1(shifter_2_out), .in2(shifter_3_out), .in3(shifter_4_out),
    .out(multiplexer_1_out), .sel(Shift_Control));  // open: en
  Multiplexer #(.width(32)) multiplexer_2 (
    .in0(multiplexer_1_out), .in1({32{1'b0}}), .out(Data_Out), .sel(and_1_out));  // open: en
endmodule

module AddressHelp (
  input  [6:0] Addr,
  output Writable,
  output [1:0] Value,
  output [1:0] Select
);

  wire and_1_out, and_2_out, and_4_out, and_5_out, and_6_out, not_1_out, not_2_out, or_1_out, or_2_out;

  or or_1 (or_1_out, Addr[6], Addr[5], Addr[4], Addr[3], Addr[2]);
  and and_1 (and_1_out, Addr[0], Addr[1]);
  and and_2 (and_2_out, Addr[2], Addr[3], Addr[4], Addr[5], Addr[6]);
  not not_1 (not_1_out, Writable);
  and and_3 (Writable, or_2_out, not_2_out);
  or or_2 (or_2_out, Addr[1], or_1_out);
  and and_4 (and_4_out, and_1_out, and_2_out);
  not not_2 (not_2_out, and_4_out);
  Priority_Encoder #(.select(2)) priority_encoder_1 (
    .in0(not_2_out), .in1(not_1_out), .in2(and_5_out), .in3(and_6_out), .out(Select));  // open: gs, en_out, en_in
  and and_5 (and_5_out, and_2_out, ~not_1_out, Addr[0]);  // AND_Gate
  and and_6 (and_6_out, Addr[1], ~not_1_out, and_2_out);  // AND_Gate

  assign Value = Addr[1:0];
endmodule

module ConditionalLogic (
  input  N,
  input  Z,
  input  C,
  input  V,
  input  [3:0] Condition,
  output Execute
);

  wire and_1_out, and_2_out, and_3_out, and_4_out, decoder_1_out0, decoder_1_out1, decoder_1_out2,
       decoder_1_out4, decoder_1_out8;

  Decoder #(.select(4)) decoder_1 (
    .out0(decoder_1_out0), .out1(decoder_1_out1), .out2(decoder_1_out2), .out4(decoder_1_out4),
    .out8(decoder_1_out8), .sel(Condition));  // open: out3, out5, out6, out7, out9, out10, out11, out12, out13, out14, out15, en
  and and_1 (and_1_out, decoder_1_out2, C);
  and and_2 (and_2_out, decoder_1_out4, Z);
  and and_3 (and_3_out, decoder_1_out8, N);
  or or_1 (Execute, decoder_1_out0, and_3_out, and_2_out, and_1_out, and_4_out);
  and and_4 (and_4_out, decoder_1_out1, V);
endmodule

module InterruptController (
  input  Call_Clear,
  input  [7:0] InrCode,
  input  [31:0] Value,
  input  Set,
  input  Reset,
  output Handle,
  output Type,
  output [6:0] Priority,
  output [23:0] HandleAddress
);

  wire and_1_out, and_2_out, comparator_1_eq, comparator_2_gt, h_q, multiplexer_2_out, not_1_out, not_2_out,
       not_3_out, or_1_out, or_2_out, or_3_out;
  wire [1:0] priority_encoder_1_out;
  wire [7:0] multiplexer_1_out, register_1_q;
  wire [31:0] multiplexer_3_out, ram_1_data;

  Register register_1 (.D(multiplexer_1_out), .en(Call_Clear), .Q(register_1_q), .clk(Call_Clear), .clr(Reset));
  Multiplexer #(.select(2), .width(8)) multiplexer_1 (
    .in0(register_1_q), .in1(InrCode), .in2(InrCode), .in3(InrCode), .out(multiplexer_1_out),
    .sel(priority_encoder_1_out));  // open: en
  and and_1 (and_1_out, or_2_out, Set);
  or or_1 (or_1_out, InrCode[0], InrCode[1], InrCode[2], InrCode[3], InrCode[4]);
  or or_2 (or_2_out, or_1_out, or_3_out);
  or or_3 (or_3_out, InrCode[5], InrCode[6], InrCode[7]);
  Comparator comparator_1 (.a(register_1_q), .b(InrCode), .eq(comparator_1_eq));  // open: gt, lt
  RAM #(.dataWidth(32), .bus("separate")) ram_1 (
    .addr(InrCode), .din(Value), .data(ram_1_data), .str(and_1_out), .clk(and_1_out), .clr(Reset));  // open: sel, ld
  Multiplexer #(.select(2)) multiplexer_2 (
    .in0(h_q), .in1(h_q), .in2(not_1_out), .in3(not_1_out), .out(multiplexer_2_out),
    .sel(priority_encoder_1_out));  // open: en
  Priority_Encoder #(.select(2)) priority_encoder_1 (
    .in0(1'b1), .in1(not_3_out), .in2(comparator_1_eq), .in3(not_1_out), .out(priority_encoder_1_out));
  Multiplexer #(.select(2), .width(32)) multiplexer_3 (
    .in0({Type, Priority, HandleAddress}), .in1(ram_1_data), .in2(ram_1_data), .in3(ram_1_data),
    .out(multiplexer_3_out), .sel(priority_encoder_1_out));  // open: en
  not not_1 (not_1_out, h_q);
  Register #(.width(1)) h (.D(multiplexer_2_out), .en(Call_Clear), .Q(h_q), .clk(Call_Clear), .clr(Reset));
  Register #(.width(32)) register_2 (
    .D(multiplexer_3_out), .en(Call_Clear), .Q({Type, Priority, HandleAddress}), .clk(Call_Clear), .clr(Reset));
  not not_2 (not_2_out, or_2_out);
  Comparator #(.width(7)) comparator_2 (.a(Priority), .b(ram_1_data[30:24]), .gt(comparator_2_gt));  // open: eq, lt
  not not_3 (not_3_out, comparator_2_gt);
  and and_2 (and_2_out, Call_Clear, not_2_out);
  or or_4 (Handle, and_2_out, h_q);
endmodule

module IOController (
  input  Write,
  input  [31:0] Address,
  input  [31:0] DataIn,
  input  [6:0] KBIn,
  input  KBNotEmpty,
  input  Read,
  input  ExeClock,
  input  Reset,
  input  [31:0] DiskDataIn,
  output [6:0] TTYOut,
  output TTYEnable,
  output KBEnable,
  output [31:0] DataOut,
  output KBRead,
  output WriteDisk,
  output [31:0] DiskAddr,
  output [31:0] DiskDataOut
);

  wire and_2_out, and_4_out, and_5_out, and_6_out, comparator_1_gt, comparator_2_gt, decoder_1_out0,
       decoder_1_out1, decoder_1_out2, decoder_1_out3, decoder_1_out4, decoder_1_out5, nor_1_out, or_1_out,
       or_2_out;
  wire [2:0] bit_extender_1_out;
  wire [31:0] adder_1_out, bit_extender_2_out, multiplexer_1_out, multiplexer_2_out, register_1_q,
       register_2_q, register_4_q;

  Comparator #(.width(32)) comparator_1 (.a(32'h1000000), .b(Address), .gt(comparator_1_gt));  // open: eq, lt
  Comparator #(.width(32)) comparator_2 (.a(Address), .b(32'h1000005), .gt(comparator_2_gt));  // open: eq, lt
  Bit_Extender #(.in_width(32), .out_width(3)) bit_extender_1 (.in(Address), .out(bit_extender_1_out));
  nor nor_1 (nor_1_out, comparator_1_gt, comparator_2_gt);
  Decoder #(.select(3), .disabled(0)) decoder_1 (
    .out0(decoder_1_out0), .out1(decoder_1_out1), .out2(decoder_1_out2), .out3(decoder_1_out3),
    .out4(decoder_1_out4), .out5(decoder_1_out5), .sel(bit_extender_1_out), .en(nor_1_out));  // open: out6, out7
  Adder #(.width(32)) adder_1 (.a(DiskAddr), .b(register_4_q), .out(adder_1_out));  // open: cin, cout
  and and_1 (WriteDisk, decoder_1_out5, Write);
  assign bit_extender_2_out = {{25{1'b0}}, KBIn};  // Bit_Extender bit_extender_2
  and and_2 (and_2_out, decoder_1_out5, Read);
  and and_3 (TTYEnable, Write, decoder_1_out0);
  and and_4 (and_4_out, Write, decoder_1_out1);
  Multiplexer #(.width(32), .enable("false")) multiplexer_1 (
    .in0({32{1'b0}}), .in1(bit_extender_2_out), .out(multiplexer_1_out), .sel(KBNotEmpty));
  Multiplexer #(.width(32), .enable("false")) multiplexer_2 (
    .in0(DataIn), .in1(adder_1_out), .out(multiplexer_2_out), .sel(or_2_out));
  or or_1 (or_1_out, or_2_out, and_5_out);
  and and_5 (and_5_out, Write, decoder_1_out3);
  and and_6 (and_6_out, Write, decoder_1_out4);
  or or_2 (or_2_out, WriteDisk, and_2_out);
  Bit_Extender #(.in_width(32), .out_width(7)) bit_extender_3 (.in(DataIn), .out(TTYOut));
  Register #(.width(32)) register_1 (.D(DataIn), .en(TTYEnable), .Q(register_1_q), .clk(ExeClock), .clr(Reset));
  Register #(.width(32)) register_2 (.D(DataIn), .en(and_4_out), .Q(register_2_q), .clk(ExeClock), .clr(Reset));
  Register #(.width(32)) register_3 (.D(multiplexer_2_out), .en(or_1_out), .Q(DiskAddr), .clk(ExeClock), .clr(Reset));
  Register #(.width(32)) register_4 (.D(DataIn), .en(and_6_out), .Q(register_4_q), .clk(ExeClock), .clr(Reset));
  Multiplexer #(.select(3), .width(32), .enable("false")) multiplexer_3 (
    .in0(register_1_q), .in1(register_2_q), .in2(multiplexer_1_out), .in3(DiskAddr), .in4(register_4_q),
    .in5(DiskDataIn), .out(DataOut), .sel(bit_extender_1_out));  // open: in6, in7
  Comparator #(.width(32), .mode("unsigned")) comparator_3 (
    .a(register_2_q), .b(32'h1), .eq(KBEnable));  // open: gt, lt
  and and_7 (KBRead, Read, decoder_1_out2);

  assign DiskDataOut = DataIn;
endmodule

module DisableGate (
  input  Disable,
  input  In,
  output Out
);

  and and_1 (Out, ~Disable, In);  // AND_Gate
endmodule
